# Fritzing sketch Wiring plan (saved by Fritzing 0.9.4)
stripboards: 1

parts:
  WeMos_D1_Mini1 = WeMos D1 Mini  # not connected
  U1 = PCF8574 [package="DIP16 [THT]"]  # not connected
  JP1 = Header 1 [package=1x01_offset]
  JP2 = Header 1 [package=1x01_offset]
  JP3 = Header 1 [package=1x01_offset]
  JP4 = Header 1 [package=1x01_offset]
  JP7 = Header 1 [package=1x01_offset]  # not connected
  JP8 = Header 1 [package=1x01_offset]
  JP9 = Header 1 [package=1x01_offset]  # not connected
  JP10 = Header 1 [package=1x01_offset]  # not connected
  JP11 = Header 1 [package=1x01_offset]
  JP12 = Header 1 [package=1x01_offset]
  JP13 = Header 1 [package=1x01_offset]
  JP14 = Header 1 [package=1x01_offset]  # not connected
  JP5 = Header 1 [package=1x01_offset]
  JP15 = Header 1 [package=1x01_offset]
  JP16 = Header 1 [package=1x01_offset]
  JP17 = Header 1 [package=1x01_offset]
  JP18 = Header 1 [package=1x01_offset]  # not connected
  JP19 = Header 1 [package=1x01_offset]
  JP20 = Header 1 [package=1x01_offset]
  JP21 = Header 1 [package=1x01_offset]
  JP22 = Header 1 [package=1x01_offset]  # not connected
  JP23 = Header 1 [package=1x01_offset]  # not connected
  JP24 = Header 1 [package=1x01_offset]  # not connected

nets:
  N1: JP1.1, JP2.1, JP3.1, JP4.1, JP15.1, JP16.1
  N2: JP8.1, JP5.1
  N3: JP11.1, JP19.1
  N4: JP12.1, JP21.1
  N5: JP13.1, JP17.1, JP20.1
